// Logisim project Proyecto ALU.circ as structural Verilog: 16 circuits, main circuit main
module main (
  input  a1,
  input  a2,
  input  in_3,
  input  a3,
  input  a4,
  input  valor0,
  input  b1,
  input  Valor1Too,
  input  b2,
  input  b3,
  input  in_11,
  input  b4,
  input  valor1,
  input  bSUMA,
  input  bRESTA,
  input  bIgual,
  input  bMayor,
  input  bMenor,
  input  bAnd,
  input  bOr,
  input  bXor,
  input  NegacionA,
  input  NegacionB
);

  wire acarr, and_1_out, andi_1_s0, andi_1_s1, andi_1_s2, andi_1_s3, D1, D2, D3, D4, D5, D6, D7,
       l_7_segmentos_6324581b_1_d1, l_7_segmentos_6324581b_1_d2, l_7_segmentos_6324581b_1_d3,
       l_7_segmentos_6324581b_1_d4, l_7_segmentos_6324581b_1_d5, l_7_segmentos_6324581b_1_d6,
       l_7_segmentos_6324581b_1_d7, l_7_segmentos_6324581b_1_ssigno, l_7_segmentos_6324581b_1_u1,
       l_7_segmentos_6324581b_1_u2, l_7_segmentos_6324581b_1_u3, l_7_segmentos_6324581b_1_u4,
       l_7_segmentos_6324581b_1_u5, l_7_segmentos_6324581b_1_u6, l_7_segmentos_6324581b_1_u7,
       multiplexer_1_out, multiplexer_2_out, multiplexer_3_out, multiplexer_4_out, multiplexer_5_out,
       multiplexer_6_out, multiplexer_7_out, multiplexer_8_out, multiplexer_9_out, multiplexer_10_out,
       multiplexer_11_out, multiplexer_12_out, multiplexer_13_out, multiplexer_14_out, multiplexer_15_out,
       multiplexer_16_out, multiplexer_17_out, multiplexer_18_out, O0, O1, O2, O3, ori_1_s0, ori_1_s1,
       ori_1_s2, ori_1_s3, RIgualQ, RMayorQ, RMenorQ, SIGNO, U1, U2, U3, U4, U5, U6, U7, x1RESTA, x1SUMA,
       x2RESTA, x2SUMA, x3RESTA, x3SUMA, x4RESTA, x4SUMA, xa1NEG, xa2NEG, xa3NEG, xa4NEG, xb1NEG, xb2NEG,
       xb3NEG, xb4NEG, xori_1_s0, xori_1_s1, xori_1_s2, xori_1_s3, xSIGNO;

  SUMA suma_1 (
    .A1(a1), .B1(b1), .A2(a2), .B2(b2), .A3(a3), .B3(b3), .A4(a4), .B4(b4), .x1(x1SUMA), .x2(x2SUMA),
    .x3(x3SUMA), .x4(x4SUMA), .acarr(acarr));  // open: vacio
  RESTA resta_1 (
    .A1(a1), .vacio2(Valor1Too), .A2(a2), .A3(a3), .A4(a4), .B1(b1), .B2(b2), .VACIO(Valor1Too), .B3(b3),
    .B4(b4), .X1(x1RESTA), .X2(x2RESTA), .X3(x3RESTA), .X4(x4RESTA), .SIGNO(xSIGNO));
  IGUALDAD igualdad_1 (.A1(a1), .A2(a2), .A3(a3), .A4(a4), .B1(b1), .B2(b2), .B3(b3), .B4(b4), .X(RIgualQ));
  MAYOR_A mayor_a_1 (.A3(a4), .A2(a3), .A1(a2), .A0(a1), .B3(b4), .B2(b3), .B1(b2), .B0(b1), .A_MAYOR_B(RMayorQ));
  MENOR_A menor_a_1 (.A3(a4), .A2(a3), .A1(a2), .A0(a1), .B3(b4), .B2(b3), .B1(b2), .B0(b1), .A_MENOR_B(RMenorQ));
  NEGACION negacion_1 (.a(a1), .b(a2), .c(a3), .d(a4), .x1(xa1NEG), .x2(xa2NEG), .x3(xa3NEG), .x4(xa4NEG));
  NEGACION negacion_2 (.a(b1), .b(b2), .c(b3), .d(b4), .x1(xb1NEG), .x2(xb2NEG), .x3(xb3NEG), .x4(xb4NEG));
  ANDI andi_1 (
    .a(a1), .b(b1), .c(a2), .d(b2), .e(a3), .f(b3), .g(a4), .h(b4), .S0(andi_1_s0), .S1(andi_1_s1),
    .S2(andi_1_s2), .S3(andi_1_s3));
  ORI ori_1 (
    .a(a1), .b(b1), .c(a2), .d(b2), .e(a3), .f(b3), .g(a4), .h(b4), .S0(ori_1_s0), .S1(ori_1_s1),
    .S2(ori_1_s2), .S3(ori_1_s3));
  XORI xori_1 (
    .a(a1), .b(b1), .c(a2), .d(b2), .e(a3), .f(b3), .g(a4), .h(b4), .S0(xori_1_s0), .S1(xori_1_s1),
    .S2(xori_1_s2), .S3(xori_1_s3));
  Multiplexer multiplexer_1 (.in0(in_3), .in1(acarr), .out(multiplexer_1_out), .sel(bSUMA));
  Multiplexer multiplexer_2 (.in0(in_3), .in1(x1SUMA), .out(multiplexer_2_out), .sel(bSUMA));
  Multiplexer multiplexer_3 (.in0(in_3), .in1(x2SUMA), .out(multiplexer_3_out), .sel(bSUMA));
  Multiplexer multiplexer_4 (.in0(in_3), .in1(x3SUMA), .out(multiplexer_4_out), .sel(bSUMA));
  Multiplexer multiplexer_5 (.in0(in_3), .in1(x4SUMA), .out(multiplexer_5_out), .sel(bSUMA));
  Multiplexer multiplexer_6 (.in0(in_3), .in1(valor1), .out(multiplexer_6_out), .sel(bSUMA));
  SelectorI selectori_1 (
    .AndSel(bAnd), .OrSel(bOr), .XorSel(bXor), .nASel(NegacionA), .nBSel(NegacionB), .And0(andi_1_s0),
    .Or0(ori_1_s0), .Xor0(xori_1_s0), .nA0(xa1NEG), .nB0(xb1NEG), .And1(andi_1_s1), .Or1(ori_1_s1),
    .Xor1(xori_1_s1), .nA1(xa2NEG), .nB1(xb2NEG), .And2(andi_1_s2), .Or2(ori_1_s2), .Xor2(xori_1_s2),
    .nA2(xa3NEG), .nB2(xb3NEG), .And3(andi_1_s3), .Or3(ori_1_s3), .Xor3(xori_1_s3), .nA3(xa4NEG),
    .nB3(xb4NEG), .O0(O0), .O1(O1), .O2(O2), .O3(O3));  // open: Vacio0
  Multiplexer multiplexer_7 (.in0(multiplexer_1_out), .in1(valor0), .out(multiplexer_7_out), .sel(bRESTA));
  Multiplexer multiplexer_8 (.in0(multiplexer_2_out), .in1(x1RESTA), .out(multiplexer_8_out), .sel(bRESTA));
  Multiplexer multiplexer_9 (.in0(multiplexer_3_out), .in1(x2RESTA), .out(multiplexer_9_out), .sel(bRESTA));
  Multiplexer multiplexer_10 (.in0(multiplexer_4_out), .in1(x3RESTA), .out(multiplexer_10_out), .sel(bRESTA));
  Multiplexer multiplexer_11 (.in0(multiplexer_5_out), .in1(x4RESTA), .out(multiplexer_11_out), .sel(bRESTA));
  Multiplexer multiplexer_12 (.in0(multiplexer_6_out), .in1(xSIGNO), .out(multiplexer_12_out), .sel(bRESTA));
  and and_1 (and_1_out, bSUMA, bRESTA);
  _7_Segment_Display u_7_segment_display_1 (.g(SIGNO));  // open: f, a, b, e, d, c, dp
  Multiplexer multiplexer_13 (.in0(multiplexer_7_out), .in1(in_3), .out(multiplexer_13_out), .sel(and_1_out));
  Multiplexer multiplexer_14 (.in0(multiplexer_8_out), .in1(in_3), .out(multiplexer_14_out), .sel(and_1_out));
  Multiplexer multiplexer_15 (.in0(multiplexer_9_out), .in1(in_3), .out(multiplexer_15_out), .sel(and_1_out));
  Multiplexer multiplexer_16 (.in0(multiplexer_10_out), .in1(in_3), .out(multiplexer_16_out), .sel(and_1_out));
  Multiplexer multiplexer_17 (.in0(multiplexer_11_out), .in1(in_3), .out(multiplexer_17_out), .sel(and_1_out));
  Multiplexer multiplexer_18 (.in0(multiplexer_12_out), .in1(in_3), .out(multiplexer_18_out), .sel(and_1_out));
  _7_Segment_Display u_7_segment_display_2 (.g(D7), .f(D6), .a(D1), .b(D2), .e(D5), .d(D4), .c(D3));  // open: dp
  L_7_SEGMENTOS_6324581b l_7_segmentos_6324581b_1 (
    .A(multiplexer_13_out), .B(multiplexer_14_out), .C(multiplexer_15_out), .D(multiplexer_16_out),
    .E(multiplexer_17_out), .SIGNO(multiplexer_18_out), .U1(l_7_segmentos_6324581b_1_u1),
    .U2(l_7_segmentos_6324581b_1_u2), .U3(l_7_segmentos_6324581b_1_u3), .U4(l_7_segmentos_6324581b_1_u4),
    .U5(l_7_segmentos_6324581b_1_u5), .U6(l_7_segmentos_6324581b_1_u6), .U7(l_7_segmentos_6324581b_1_u7),
    .D1(l_7_segmentos_6324581b_1_d1), .D2(l_7_segmentos_6324581b_1_d2), .D3(l_7_segmentos_6324581b_1_d3),
    .D4(l_7_segmentos_6324581b_1_d4), .D5(l_7_segmentos_6324581b_1_d5), .D6(l_7_segmentos_6324581b_1_d6),
    .D7(l_7_segmentos_6324581b_1_d7), .sSIGNO(l_7_segmentos_6324581b_1_ssigno));
  _7_Segment_Display u_7_segment_display_3 (.g(U7), .f(U6), .a(U1), .b(U2), .e(U5), .d(U4), .c(U3));  // open: dp
  LED led_1 (.in(O0));
  LED led_2 (.in(O1));
  LED led_3 (.in(O2));
  SelectorComp selectorcomp_1 (
    .RMayorQ(RMayorQ), .RMenorQ(RMenorQ), .RIgualQ(RIgualQ), .U1(l_7_segmentos_6324581b_1_u1),
    .U2(l_7_segmentos_6324581b_1_u2), .U3(l_7_segmentos_6324581b_1_u3), .U4(l_7_segmentos_6324581b_1_u4),
    .U5(l_7_segmentos_6324581b_1_u5), .U6(l_7_segmentos_6324581b_1_u6), .U7(l_7_segmentos_6324581b_1_u7),
    .D1(l_7_segmentos_6324581b_1_d1), .D2(l_7_segmentos_6324581b_1_d2), .D3(l_7_segmentos_6324581b_1_d3),
    .VALOR0(in_11), .D4(l_7_segmentos_6324581b_1_d4), .D5(l_7_segmentos_6324581b_1_d5),
    .D6(l_7_segmentos_6324581b_1_d6), .D7(l_7_segmentos_6324581b_1_d7),
    .Signo(l_7_segmentos_6324581b_1_ssigno), .Mayor(bMayor), .Menor(bMenor), .Igual(bIgual), .RU1(U1),
    .RU2(U2), .RU3(U3), .RU4(U4), .RU5(U5), .RU6(U6), .RU7(U7), .RD1(D1), .RD2(D2), .RD3(D3), .RD4(D4),
    .RD5(D5), .RD6(D6), .RD7(D7), .RSIGNO(SIGNO));
  LED led_4 (.in(O3));

  // Other names for the same wires on the sheet: a = a1; b = a2; c = a3; d = a4; e = b1; f = b2; g = b3; h = b4;
  //   igualq = bIgual; mayorq = bMayor; menorq = bMenor; nA = NegacionA; nB = NegacionB
endmodule

module SUMA (
  input  A1,
  input  A2,
  input  A3,
  input  A4,
  input  vacio,
  input  B1,
  input  B2,
  input  B3,
  input  B4,
  output x3,
  output x4,
  output x1,
  output x2,
  output acarr
);

  wire a, b, c;

  SUMA_SIMPLE suma_simple_1 (.A(A4), .B(B4), .in_3(vacio), .X(x4), .Acarr(a));
  SUMA_SIMPLE suma_simple_2 (.A(A3), .B(B3), .in_3(a), .X(x3), .Acarr(b));
  SUMA_SIMPLE suma_simple_3 (.A(A2), .B(B2), .in_3(b), .X(x2), .Acarr(c));
  SUMA_SIMPLE suma_simple_4 (.A(A1), .B(B1), .in_3(c), .X(x1), .Acarr(acarr));
endmodule

module SUMA_SIMPLE (
  input  A,
  input  B,
  input  in_3,
  output X,
  output Acarr
);

  wire and_1_out, and_2_out, and_3_out, and_4_out, and_5_out, and_6_out, and_7_out, not_1_out, not_2_out,
       not_3_out, not_4_out, not_5_out, not_6_out;

  not not_1 (not_1_out, A);
  not not_2 (not_2_out, B);
  not not_3 (not_3_out, A);
  not not_4 (not_4_out, in_3);
  not not_5 (not_5_out, B);
  not not_6 (not_6_out, in_3);
  and and_1 (and_1_out, B, in_3);
  and and_2 (and_2_out, A, in_3);
  and and_3 (and_3_out, A, B);
  and and_4 (and_4_out, not_1_out, not_2_out, in_3);
  and and_5 (and_5_out, not_3_out, B, not_4_out);
  and and_6 (and_6_out, A, not_5_out, not_6_out);
  and and_7 (and_7_out, A, B, in_3);
  or or_1 (Acarr, and_1_out, and_2_out, and_3_out);
  or or_2 (X, and_4_out, and_5_out, and_6_out, and_7_out);
endmodule

module L_7_SEGMENTOS_6324581b (
  input  A,
  input  B,
  input  C,
  input  D,
  input  E,
  input  SIGNO,
  output U1,
  output U2,
  output U3,
  output U4,
  output U5,
  output U6,
  output U7,
  output D1,
  output D2,
  output D3,
  output D4,
  output D5,
  output D6,
  output D7,
  output sSIGNO
);

  wire and_1_out, and_2_out, and_3_out, and_4_out, and_5_out, and_6_out, and_7_out, and_8_out, and_9_out,
       and_10_out, and_11_out, and_12_out, and_13_out, and_14_out, and_15_out, and_16_out, and_17_out,
       and_18_out, and_19_out, and_20_out, and_21_out, and_22_out, and_23_out, and_24_out, and_25_out,
       and_26_out, and_27_out, and_28_out, and_29_out, and_30_out, and_31_out, and_32_out, and_33_out,
       and_34_out, and_35_out, and_36_out, and_37_out, and_38_out, and_39_out, and_40_out, and_41_out,
       and_42_out, and_43_out, and_44_out, and_45_out, and_46_out, and_47_out, and_48_out, and_49_out,
       and_50_out, and_51_out, and_52_out, and_53_out, and_54_out, and_55_out, and_56_out, and_57_out,
       and_58_out, and_59_out, and_60_out, and_61_out, and_62_out, and_63_out, and_64_out, and_65_out,
       and_66_out, and_67_out, and_68_out, and_69_out, and_70_out, and_71_out, and_72_out, and_73_out,
       and_74_out, and_75_out, not_1_out, not_2_out, not_3_out, not_4_out, not_5_out;

  not not_1 (not_1_out, A);
  not not_2 (not_2_out, B);
  not not_3 (not_3_out, C);
  not not_4 (not_4_out, D);
  not not_5 (not_5_out, E);
  and and_1 (and_1_out, not_1_out, not_3_out, not_5_out);
  and and_2 (and_2_out, not_2_out, D);
  and and_3 (and_3_out, not_1_out, C, E);
  and and_4 (and_4_out, not_1_out, B, not_4_out);
  and and_5 (and_5_out, B, C, not_4_out);
  and and_6 (and_6_out, A, not_2_out, not_5_out);
  and and_7 (and_7_out, A, not_3_out, E);
  and and_8 (and_8_out, A, D, not_5_out);
  and and_9 (and_9_out, not_1_out, not_3_out);
  and and_10 (and_10_out, not_1_out, not_4_out, not_5_out);
  and and_11 (and_11_out, not_2_out, not_3_out, E);
  and and_12 (and_12_out, not_2_out, not_3_out, D);
  and and_13 (and_13_out, not_2_out, D, E);
  and and_14 (and_14_out, not_3_out, D, E);
  and and_15 (and_15_out, B, not_4_out, not_5_out);
  and and_16 (and_16_out, B, C, not_4_out);
  and and_17 (and_17_out, B, C, not_5_out);
  and and_18 (and_18_out, A, not_2_out, C);
  and and_19 (and_19_out, not_2_out, not_4_out);
  and and_20 (and_20_out, not_3_out, not_4_out);
  and and_21 (and_21_out, not_1_out, not_2_out, C);
  and and_22 (and_22_out, B, D);
  and and_23 (and_23_out, A, not_3_out);
  and and_24 (and_24_out, A, not_4_out);
  and and_25 (and_25_out, not_1_out, not_3_out, not_5_out);
  and and_26 (and_26_out, not_2_out, not_3_out, not_5_out);
  and and_27 (and_27_out, not_2_out, not_3_out, D);
  and and_28 (and_28_out, not_2_out, D, not_5_out);
  and and_29 (and_29_out, not_3_out, D, not_5_out);
  and and_30 (and_30_out, not_1_out, C, not_4_out, E);
  and and_31 (and_31_out, not_1_out, B, not_4_out);
  and and_32 (and_32_out, B, not_4_out, E);
  and and_33 (and_33_out, B, C, E);
  and and_34 (and_34_out, A, not_2_out, D);
  and and_35 (and_35_out, A, C, not_5_out);
  and and_36 (and_36_out, not_1_out, not_3_out, not_5_out);
  and and_37 (and_37_out, not_2_out, not_3_out, not_5_out);
  and and_38 (and_38_out, not_2_out, D, not_5_out);
  and and_39 (and_39_out, not_3_out, D, not_5_out);
  and and_40 (and_40_out, not_1_out, B, not_4_out, not_5_out);
  and and_41 (and_41_out, A, C, not_5_out);
  and and_42 (and_42_out, not_2_out, not_4_out, not_5_out);
  and and_43 (and_43_out, not_1_out, not_2_out, C, not_4_out);
  and and_44 (and_44_out, not_1_out, not_2_out, C, not_5_out);
  and and_45 (and_45_out, B, not_3_out, not_4_out);
  and and_46 (and_46_out, B, D, not_5_out);
  and and_47 (and_47_out, not_1_out, B, C, D);
  and and_48 (and_48_out, A, not_2_out, not_3_out, D);
  and and_49 (and_49_out, A, B, not_4_out);
  and and_50 (and_50_out, not_2_out, not_3_out, D);
  and and_51 (and_51_out, not_2_out, D, not_5_out);
  and and_52 (and_52_out, not_1_out, C, not_4_out);
  and and_53 (and_53_out, B, not_4_out);
  and and_54 (and_54_out, not_1_out, B, C);
  and and_55 (and_55_out, A, not_3_out, not_5_out);
  and and_56 (and_56_out, A, not_2_out, D);
  and and_57 (and_57_out, not_1_out, not_2_out);
  and and_58 (and_58_out, A, B);
  and and_59 (and_59_out, not_1_out, not_3_out, not_4_out);
  and and_60 (and_60_out, A, C);
  and and_61 (and_61_out, not_2_out, not_3_out);
  and and_62 (and_62_out, B, C, D);
  and and_63 (and_63_out, not_1_out, not_2_out);
  and and_64 (and_64_out, A, B);
  and and_65 (and_65_out, not_1_out, not_3_out, not_4_out);
  and and_66 (and_66_out, A, C);
  and and_67 (and_67_out, not_1_out, not_2_out);
  and and_68 (and_68_out, not_2_out, C);
  and and_69 (and_69_out, A, B, not_3_out);
  and and_70 (and_70_out, not_1_out, not_3_out, not_4_out);
  and and_71 (and_71_out, A, C, not_4_out);
  and and_72 (and_72_out, not_1_out, not_2_out);
  and and_73 (and_73_out, not_1_out, not_3_out, not_4_out);
  and and_74 (and_74_out, A, C);
  and and_75 (and_75_out, A, B);
  or or_1 (U1, and_1_out, and_2_out, and_3_out, and_4_out, and_5_out, and_6_out, and_7_out, and_8_out);
  or or_2 (U2, and_9_out, and_10_out, and_11_out, and_12_out, and_13_out, and_14_out, and_15_out, and_16_out, and_17_out, and_18_out);
  or or_3 (U3, and_19_out, and_20_out, E, and_21_out, and_22_out, and_23_out, and_24_out);
  or or_4 (U4, and_25_out, and_26_out, and_27_out, and_28_out, and_29_out, and_30_out, and_31_out, and_32_out, and_33_out, and_34_out, and_35_out);
  or or_5 (U5, and_36_out, and_37_out, and_38_out, and_39_out, and_40_out, and_41_out);
  or or_6 (U6, and_42_out, and_43_out, and_44_out, and_45_out, and_46_out, and_47_out, and_48_out, and_49_out);
  or or_7 (U7, and_50_out, and_51_out, and_52_out, and_53_out, and_54_out, and_55_out, and_56_out);
  or or_8 (D1, and_57_out, and_58_out, and_59_out, and_60_out);
  or or_9 (D3, not_1_out, and_61_out, and_62_out);
  or or_10 (D4, and_63_out, and_64_out, and_65_out, and_66_out);
  or or_11 (D5, and_67_out, and_68_out, and_69_out, and_70_out, and_71_out);
  or or_12 (D6, and_72_out, and_73_out);
  or or_13 (D7, and_74_out, and_75_out);
  not not_6 (sSIGNO, SIGNO);

  assign D2 = 1'b1;
endmodule

module RESTA (
  input  A1,
  input  vacio2,
  input  A2,
  input  A3,
  input  A4,
  input  B1,
  input  B2,
  input  VACIO,
  input  B3,
  input  B4,
  output X1,
  output X2,
  output X3,
  output X4,
  output SIGNO
);

  wire C1, C2, C3, C4, e, f, g, h, multiplexer_1_out, multiplexer_2_out, multiplexer_3_out,
       multiplexer_4_out, negacion_1_x1, negacion_1_x2, negacion_1_x3, negacion_1_x4, negacion_2_x1,
       negacion_2_x2, negacion_2_x3, negacion_2_x4, neutro, signo_t, suma_2_x1, suma_2_x2, suma_2_x3,
       suma_2_x4;

  nor nor_1 (neutro, B4, B3, B2, B1);
  NEGACION negacion_1 (
    .a(B1), .b(B2), .c(B3), .d(B4), .x1(negacion_1_x1), .x2(negacion_1_x2), .x3(negacion_1_x3),
    .x4(negacion_1_x4));
  NEGACION negacion_2 (
    .a(C1), .b(C2), .c(C3), .d(C4), .x1(negacion_2_x1), .x2(negacion_2_x2), .x3(negacion_2_x3),
    .x4(negacion_2_x4));
  SUMA suma_1 (
    .A1(negacion_1_x1), .A2(negacion_1_x2), .A3(negacion_1_x3), .A4(negacion_1_x4), .B4(VACIO), .x1(e),
    .x2(f), .x3(g), .x4(h));  // open: vacio, B1, B2, B3, acarr
  SUMA suma_2 (
    .A1(negacion_2_x1), .A2(negacion_2_x2), .A3(negacion_2_x3), .A4(negacion_2_x4), .B4(vacio2),
    .x1(suma_2_x1), .x2(suma_2_x2), .x3(suma_2_x3), .x4(suma_2_x4));  // open: vacio, B1, B2, B3, acarr
  SUMA suma_3 (
    .A1(A1), .B1(e), .A2(A2), .B2(f), .A3(A3), .B3(g), .A4(A4), .B4(h), .x1(C1), .x2(C2), .x3(C3), .x4(C4),
    .acarr(signo_t));  // open: vacio
  Multiplexer multiplexer_1 (.in0(suma_2_x1), .in1(C1), .out(multiplexer_1_out), .sel(signo_t));
  Multiplexer multiplexer_2 (.in0(suma_2_x2), .in1(C2), .out(multiplexer_2_out), .sel(signo_t));
  Multiplexer multiplexer_3 (.in0(suma_2_x3), .in1(C3), .out(multiplexer_3_out), .sel(signo_t));
  Multiplexer multiplexer_4 (.in0(suma_2_x4), .in1(C4), .out(multiplexer_4_out), .sel(signo_t));
  Multiplexer multiplexer_5 (.in0(multiplexer_1_out), .in1(A1), .out(X1), .sel(neutro));
  Multiplexer multiplexer_6 (.in0(multiplexer_2_out), .in1(A2), .out(X2), .sel(neutro));
  Multiplexer multiplexer_7 (.in0(multiplexer_3_out), .in1(A3), .out(X3), .sel(neutro));
  Multiplexer multiplexer_8 (.in0(multiplexer_4_out), .in1(A4), .out(X4), .sel(neutro));
  Multiplexer multiplexer_9 (.in0(signo_t), .in1(neutro), .out(SIGNO), .sel(neutro));

  // Other names for the same wires on the sheet: a = A1; b = A2; c = A3; d = A4; salida1 = C1; salida2 = C2;
  //   salida3 = C3; salida4 = C4
endmodule

module NEGACION (
  input  a,
  input  b,
  input  c,
  input  d,
  output x1,
  output x2,
  output x3,
  output x4
);

  not not_1 (x1, a);
  not not_2 (x2, b);
  not not_3 (x3, c);
  not not_4 (x4, d);
endmodule

module IGUALDAD (
  input  A1,
  input  A2,
  input  A3,
  input  A4,
  input  B1,
  input  B2,
  input  B3,
  input  B4,
  output X
);

  wire xnor_1_out, xnor_2_out, xnor_3_out, xnor_4_out;

  xnor xnor_1 (xnor_1_out, A1, B1);
  xnor xnor_2 (xnor_2_out, A2, B2);
  xnor xnor_3 (xnor_3_out, A3, B3);
  xnor xnor_4 (xnor_4_out, A4, B4);
  and and_1 (X, xnor_1_out, xnor_2_out, xnor_3_out, xnor_4_out);
endmodule

module MAYOR_A (
  input  A3,
  input  A2,
  input  A1,
  input  A0,
  input  B3,
  input  B2,
  input  B1,
  input  B0,
  output A_MAYOR_B
);

  wire not_1_out, not_2_out, not_3_out, not_4_out, or_1_out, or_2_out, or_3_out, or_4_out, or_5_out,
       or_6_out, or_7_out, or_8_out, or_9_out, or_10_out, or_11_out, or_12_out, or_13_out, or_14_out,
       or_15_out, or_16_out, or_17_out, or_18_out, or_19_out, or_20_out, or_21_out, or_22_out, or_23_out;

  not not_1 (not_1_out, B3);
  not not_2 (not_2_out, B2);
  not not_3 (not_3_out, B1);
  not not_4 (not_4_out, B0);
  or or_1 (or_1_out, A3, A2, A1, A0);
  or or_2 (or_2_out, A3, A2, A1, not_4_out);
  or or_3 (or_3_out, A3, A2, A1, not_3_out);
  or or_4 (or_4_out, A3, A2, not_2_out);
  or or_5 (or_5_out, A3, not_1_out);
  or or_6 (or_6_out, A3, A2, A0, not_3_out);
  or or_7 (or_7_out, A3, A2, not_3_out, not_4_out);
  or or_8 (or_8_out, A3, A1, A0, not_2_out);
  or or_9 (or_9_out, A3, A1, not_2_out, not_4_out);
  or or_10 (or_10_out, A3, A1, not_2_out, not_3_out);
  or or_11 (or_11_out, A3, A0, not_2_out, not_3_out);
  or or_12 (or_12_out, A3, not_2_out, not_3_out, not_4_out);
  or or_13 (or_13_out, A2, A1, A0, not_1_out);
  or or_14 (or_14_out, A2, A1, not_1_out, not_4_out);
  or or_15 (or_15_out, A2, A1, not_1_out, not_3_out);
  or or_16 (or_16_out, A2, not_1_out, not_2_out);
  or or_17 (or_17_out, A2, A0, not_1_out, not_3_out);
  or or_18 (or_18_out, A2, not_1_out, not_3_out, not_4_out);
  or or_19 (or_19_out, A1, A0, not_1_out, not_2_out);
  or or_20 (or_20_out, A1, not_1_out, not_2_out, not_4_out);
  or or_21 (or_21_out, A1, not_1_out, not_2_out, not_3_out);
  or or_22 (or_22_out, A0, not_1_out, not_2_out, not_3_out);
  or or_23 (or_23_out, not_1_out, not_2_out, not_3_out, not_4_out);
  and and_1 (A_MAYOR_B, or_1_out, or_2_out, or_3_out, or_4_out, or_5_out, or_6_out, or_7_out, or_8_out, or_9_out, or_10_out, or_11_out, or_12_out, or_13_out, or_14_out, or_15_out, or_16_out, or_17_out, or_18_out, or_19_out, or_20_out, or_21_out, or_22_out, or_23_out);
endmodule

module MENOR_A (
  input  A3,
  input  A2,
  input  A1,
  input  A0,
  input  B3,
  input  B2,
  input  B1,
  input  B0,
  output A_MENOR_B
);

  wire igualdad_1_x, mayor_a_1_a_mayor_b, not_1_out, not_2_out;

  MAYOR_A mayor_a_1 (
    .A3(A3), .A2(A2), .A1(A1), .A0(A0), .B3(B3), .B2(B2), .B1(B1), .B0(B0), .A_MAYOR_B(mayor_a_1_a_mayor_b));
  IGUALDAD igualdad_1 (.A1(A3), .A2(A2), .A3(A1), .A4(A0), .B1(B3), .B2(B2), .B3(B1), .B4(B0), .X(igualdad_1_x));
  not not_1 (not_1_out, mayor_a_1_a_mayor_b);
  not not_2 (not_2_out, igualdad_1_x);
  and and_1 (A_MENOR_B, not_1_out, not_2_out);
endmodule

module ANDI (
  input  a,
  input  b,
  input  c,
  input  d,
  input  e,
  input  f,
  input  g,
  input  h,
  output S0,
  output S1,
  output S2,
  output S3
);

  and and_1 (S0, a, b);
  and and_2 (S1, c, d);
  and and_3 (S2, e, f);
  and and_4 (S3, g, h);
endmodule

module ORI (
  input  a,
  input  b,
  input  c,
  input  d,
  input  e,
  input  f,
  input  g,
  input  h,
  output S0,
  output S1,
  output S2,
  output S3
);

  or or_1 (S0, b, a);
  or or_2 (S1, d, c);
  or or_3 (S2, f, e);
  or or_4 (S3, h, g);
endmodule

module XORI (
  input  a,
  input  b,
  input  c,
  input  d,
  input  e,
  input  f,
  input  g,
  input  h,
  output S0,
  output S1,
  output S2,
  output S3
);

  xor xor_1 (S0, b, a);
  xor xor_2 (S1, d, c);
  xor xor_3 (S2, f, e);
  xor xor_4 (S3, h, g);
endmodule

module SelectorI (
  input  AndSel,
  input  OrSel,
  input  XorSel,
  input  nASel,
  input  nBSel,
  input  And0,
  input  Or0,
  input  Xor0,
  input  nA0,
  input  nB0,
  input  And1,
  input  Or1,
  input  Xor1,
  input  nA1,
  input  nB1,
  input  And2,
  input  Or2,
  input  Xor2,
  input  nA2,
  input  nB2,
  input  And3,
  input  Or3,
  input  Xor3,
  input  nA3,
  input  nB3,
  input  Vacio0,
  output O0,
  output O1,
  output O2,
  output O3
);

  wire and_1_out, and_2_out, and_3_out, and_4_out, and_5_out, and_6_out, and_7_out, and_8_out, and_9_out,
       and_10_out, and_11_out, and_12_out, and_13_out, and_14_out, and_15_out, and_16_out, and_17_out,
       and_18_out, and_19_out, and_20_out, or_1_out, or_2_out, or_3_out, or_4_out, validacionselector_1_x,
       validacionselector_2_x, validacionselector_3_x, validacionselector_4_x;

  and and_1 (and_1_out, And0, AndSel);
  and and_2 (and_2_out, Or0, OrSel);
  and and_3 (and_3_out, Xor0, XorSel);
  and and_4 (and_4_out, nA0, nASel);
  and and_5 (and_5_out, nB0, nBSel);
  and and_6 (and_6_out, And1, AndSel);
  and and_7 (and_7_out, Or1, OrSel);
  and and_8 (and_8_out, Xor1, XorSel);
  and and_9 (and_9_out, nA1, nASel);
  and and_10 (and_10_out, nB1, nBSel);
  and and_11 (and_11_out, And2, AndSel);
  and and_12 (and_12_out, Or2, OrSel);
  and and_13 (and_13_out, Xor2, XorSel);
  and and_14 (and_14_out, nA2, nASel);
  and and_15 (and_15_out, nB2, nBSel);
  and and_16 (and_16_out, And3, AndSel);
  and and_17 (and_17_out, Or3, OrSel);
  and and_18 (and_18_out, Xor3, XorSel);
  and and_19 (and_19_out, nA3, nASel);
  and and_20 (and_20_out, nB3, nBSel);
  or or_1 (or_1_out, and_1_out, and_2_out, and_3_out, and_4_out, and_5_out);
  or or_2 (or_2_out, and_6_out, and_7_out, and_8_out, and_9_out, and_10_out);
  or or_3 (or_3_out, and_11_out, and_12_out, and_13_out, and_14_out, and_15_out);
  or or_4 (or_4_out, and_16_out, and_17_out, and_18_out, and_19_out, and_20_out);
  Multiplexer multiplexer_1 (.in0(or_1_out), .in1(Vacio0), .out(O0), .sel(validacionselector_1_x));
  ValidacionSelector validacionselector_1 (
    .a(AndSel), .b(OrSel), .c(XorSel), .d(nASel), .e(nBSel), .x(validacionselector_1_x));
  Multiplexer multiplexer_2 (.in0(or_2_out), .in1(Vacio0), .out(O1), .sel(validacionselector_2_x));
  ValidacionSelector validacionselector_2 (
    .a(AndSel), .b(OrSel), .c(XorSel), .d(nASel), .e(nBSel), .x(validacionselector_2_x));
  Multiplexer multiplexer_3 (.in0(or_3_out), .in1(Vacio0), .out(O2), .sel(validacionselector_3_x));
  ValidacionSelector validacionselector_3 (
    .a(AndSel), .b(OrSel), .c(XorSel), .d(nASel), .e(nBSel), .x(validacionselector_3_x));
  Multiplexer multiplexer_4 (.in0(or_4_out), .in1(Vacio0), .out(O3), .sel(validacionselector_4_x));
  ValidacionSelector validacionselector_4 (
    .a(AndSel), .b(OrSel), .c(XorSel), .d(nASel), .e(nBSel), .x(validacionselector_4_x));

  // Other names for the same wires on the sheet: AS = AndSel; nA = nASel; nB = nBSel; OS = OrSel; XS = XorSel
endmodule

module L_7SegmentosComparacion (
  input  resultado,
  input  mayor,
  input  menor,
  input  igual,
  output s1,
  output s2,
  output s3,
  output s4,
  output s5,
  output s6,
  output s7,
  output r1,
  output r2,
  output r3,
  output r4,
  output r5,
  output r6,
  output r7
);

  wire and_3_out, and_4_out, and_5_out, and_6_out, and_7_out, and_8_out, and_9_out, and_10_out, and_11_out,
       and_12_out, and_13_out, and_14_out, and_15_out, and_16_out, and_17_out, and_18_out, and_19_out,
       and_20_out, and_21_out, and_22_out, and_23_out, and_24_out, not_1_out, not_2_out, not_3_out, not_4_out;

  not not_1 (not_1_out, resultado);
  not not_2 (not_2_out, mayor);
  not not_3 (not_3_out, menor);
  not not_4 (not_4_out, igual);
  or or_1 (s1, not_4_out, menor, mayor);
  and and_1 (s2, mayor, not_3_out, not_4_out);
  and and_2 (s3, mayor, not_3_out, not_4_out);
  and and_3 (and_3_out, not_1_out, not_2_out, not_4_out);
  and and_4 (and_4_out, mayor, igual);
  and and_5 (and_5_out, not_1_out, not_2_out, not_4_out);
  and and_6 (and_6_out, mayor, igual);
  and and_7 (and_7_out, not_1_out, not_2_out, not_3_out);
  and and_8 (and_8_out, mayor, menor);
  and and_9 (and_9_out, menor, igual);
  and and_10 (and_10_out, mayor, igual);
  and and_11 (and_11_out, mayor, menor);
  and and_12 (and_12_out, resultado, not_2_out, not_3_out);
  and and_13 (and_13_out, resultado, not_2_out, not_4_out);
  and and_14 (and_14_out, resultado, not_3_out, not_4_out);
  and and_15 (and_15_out, resultado, not_2_out, not_3_out);
  and and_16 (and_16_out, resultado, not_2_out, not_4_out);
  and and_17 (and_17_out, resultado, not_3_out, not_4_out);
  and and_18 (and_18_out, not_2_out, not_3_out, not_4_out);
  and and_19 (and_19_out, menor, igual);
  and and_20 (and_20_out, mayor, igual);
  and and_21 (and_21_out, mayor, menor);
  and and_22 (and_22_out, menor, igual);
  and and_23 (and_23_out, mayor, igual);
  and and_24 (and_24_out, mayor, menor);
  or or_2 (s5, and_3_out, menor, and_4_out);
  or or_3 (s6, and_5_out, menor, and_6_out);
  or or_4 (s7, and_7_out, igual, and_8_out);
  or or_5 (r1, not_1_out, and_9_out, and_10_out, and_11_out);
  or or_6 (r2, and_12_out, and_13_out, and_14_out);
  or or_7 (r3, and_15_out, and_16_out, and_17_out);
  or or_8 (r4, and_18_out, and_19_out, and_20_out, and_21_out, resultado);
  or or_9 (r7, not_1_out, and_22_out, and_23_out, and_24_out);

  assign r5 = 1'b1;
  assign r6 = 1'b1;
  assign s4 = 1'b1;
endmodule

module SelectorComp (
  input  RMayorQ,
  input  RMenorQ,
  input  RIgualQ,
  input  U1,
  input  U2,
  input  U3,
  input  U4,
  input  U5,
  input  U6,
  input  U7,
  input  D1,
  input  D2,
  input  D3,
  input  VALOR0,
  input  D4,
  input  D5,
  input  D6,
  input  D7,
  input  Signo,
  input  Mayor,
  input  Menor,
  input  Igual,
  output RU1,
  output RU2,
  output RU3,
  output RU4,
  output RU5,
  output RU6,
  output RU7,
  output RD1,
  output RD2,
  output RD3,
  output RD4,
  output RD5,
  output RD6,
  output RD7,
  output RSIGNO
);

  wire l_7segmentoscomparacion_1_r1, l_7segmentoscomparacion_1_r2, l_7segmentoscomparacion_1_r3,
       l_7segmentoscomparacion_1_r4, l_7segmentoscomparacion_1_r5, l_7segmentoscomparacion_1_r6,
       l_7segmentoscomparacion_1_r7, l_7segmentoscomparacion_1_s1, l_7segmentoscomparacion_1_s2,
       l_7segmentoscomparacion_1_s3, l_7segmentoscomparacion_1_s4, l_7segmentoscomparacion_1_s5,
       l_7segmentoscomparacion_1_s6, l_7segmentoscomparacion_1_s7, multiplexer_1_out, multiplexer_2_out,
       multiplexer_3_out, or_1_out;

  Multiplexer multiplexer_1 (.in0(RMenorQ), .in1(RMayorQ), .out(multiplexer_1_out), .sel(Mayor));
  Multiplexer multiplexer_2 (.in0(multiplexer_1_out), .in1(RMenorQ), .out(multiplexer_2_out), .sel(Menor));
  Multiplexer multiplexer_3 (.in0(multiplexer_2_out), .in1(RIgualQ), .out(multiplexer_3_out), .sel(Igual));
  L_7SegmentosComparacion l_7segmentoscomparacion_1 (
    .resultado(multiplexer_3_out), .mayor(Mayor), .menor(Menor), .igual(Igual),
    .s1(l_7segmentoscomparacion_1_s1), .s2(l_7segmentoscomparacion_1_s2), .s3(l_7segmentoscomparacion_1_s3),
    .s4(l_7segmentoscomparacion_1_s4), .s5(l_7segmentoscomparacion_1_s5), .s6(l_7segmentoscomparacion_1_s6),
    .s7(l_7segmentoscomparacion_1_s7), .r1(l_7segmentoscomparacion_1_r1), .r2(l_7segmentoscomparacion_1_r2),
    .r3(l_7segmentoscomparacion_1_r3), .r4(l_7segmentoscomparacion_1_r4), .r5(l_7segmentoscomparacion_1_r5),
    .r6(l_7segmentoscomparacion_1_r6), .r7(l_7segmentoscomparacion_1_r7));
  or or_1 (or_1_out, Mayor, Menor, Igual);
  Multiplexer multiplexer_4 (.in0(U1), .in1(l_7segmentoscomparacion_1_r1), .out(RU1), .sel(or_1_out));
  Multiplexer multiplexer_5 (.in0(U2), .in1(l_7segmentoscomparacion_1_r2), .out(RU2), .sel(or_1_out));
  Multiplexer multiplexer_6 (.in0(U3), .in1(l_7segmentoscomparacion_1_r3), .out(RU3), .sel(or_1_out));
  Multiplexer multiplexer_7 (.in0(U4), .in1(l_7segmentoscomparacion_1_r4), .out(RU4), .sel(or_1_out));
  Multiplexer multiplexer_8 (.in0(U5), .in1(l_7segmentoscomparacion_1_r5), .out(RU5), .sel(or_1_out));
  Multiplexer multiplexer_9 (.in0(U6), .in1(l_7segmentoscomparacion_1_r6), .out(RU6), .sel(or_1_out));
  Multiplexer multiplexer_10 (.in0(U7), .in1(l_7segmentoscomparacion_1_r7), .out(RU7), .sel(or_1_out));
  Multiplexer multiplexer_11 (.in0(D1), .in1(l_7segmentoscomparacion_1_s1), .out(RD1), .sel(or_1_out));
  Multiplexer multiplexer_12 (.in0(D2), .in1(l_7segmentoscomparacion_1_s2), .out(RD2), .sel(or_1_out));
  Multiplexer multiplexer_13 (.in0(D3), .in1(l_7segmentoscomparacion_1_s3), .out(RD3), .sel(or_1_out));
  Multiplexer multiplexer_14 (.in0(D4), .in1(l_7segmentoscomparacion_1_s4), .out(RD4), .sel(or_1_out));
  Multiplexer multiplexer_15 (.in0(D5), .in1(l_7segmentoscomparacion_1_s5), .out(RD5), .sel(or_1_out));
  Multiplexer multiplexer_16 (.in0(D6), .in1(l_7segmentoscomparacion_1_s6), .out(RD6), .sel(or_1_out));
  Multiplexer multiplexer_17 (.in0(D7), .in1(l_7segmentoscomparacion_1_s7), .out(RD7), .sel(or_1_out));
  Multiplexer multiplexer_18 (.in0(Signo), .in1(VALOR0), .out(RSIGNO), .sel(or_1_out));
endmodule

module ValidacionSelector (
  input  a,
  input  b,
  input  c,
  input  d,
  input  e,
  output x
);

  wire and_1_out, and_2_out, and_3_out, and_4_out, and_5_out, not_1_out, not_2_out, not_3_out, not_4_out,
       not_5_out, or_1_out;

  not not_1 (not_1_out, a);
  not not_2 (not_2_out, b);
  not not_3 (not_3_out, c);
  not not_4 (not_4_out, d);
  not not_5 (not_5_out, e);
  and and_1 (and_1_out, not_2_out, not_3_out, not_4_out, not_5_out);
  and and_2 (and_2_out, not_1_out, not_2_out, not_3_out, not_4_out);
  and and_3 (and_3_out, not_1_out, not_2_out, not_3_out, not_5_out);
  and and_4 (and_4_out, not_1_out, not_2_out, not_4_out, not_5_out);
  and and_5 (and_5_out, not_1_out, not_3_out, not_4_out, not_5_out);
  or or_1 (or_1_out, and_1_out, and_2_out, and_3_out, and_4_out, and_5_out);
  not not_6 (x, or_1_out);
endmodule
